// Logisim project Binary Counter  - Both Digits - no Enable Bit.circ as structural Verilog: 1 circuit, main circuit main
module main (
  input  in_1,
  input  in_2,
  input  in_3,
  input  in_4
);

  wire A_C_out, A_prime_B_prime_C_prime_AB_prime_C_out, A_prime_B_prime_C_prime_out, A_prime_B_prime_out,
       A_prime_BC_D_prime_A_C_out, A_prime_BC_out, A_prime_BC_prime_D_out, A_prime_BCD_out,
       A_prime_BCD_prime_out, A_prime_C_prime_D_prime_out, A_prime_CD_prime_2_out,
       A_prime_CD_prime_AC_prime_B_D_out, A_prime_CD_prime_out, AB_CD_C_prime_D_prime_out, AB_prime_C_out,
       AB_prime_C_prime_D_A_prime_BCD_prime_out, AB_prime_C_prime_D_out, AB_prime_C_prime_out,
       ABCD__prime_out, ABCD_A_prime_B_prime_A_prime_C_prime_D_prime_out, ABCD_out, AC_prime_B_D_out,
       B_D_out, C_AD__prime___AB_C_prime_D_prime_CD__BD_AC__prime_out, C_prime_D_prime_out,
       CD_C_prime_D_prime_out, CD_out, D_prime___AB_prime_C_prime_out, D_prime_A_C_out, not_1_out, not_2_out,
       not_3_out, not_4_out, not_5_out, not_6_out, not_7_out, not_8_out, not_9_out, not_10_out, not_11_out,
       not_12_out, not_13_out, not_14_out, not_15_out, not_16_out, not_17_out, not_18_out, not_19_out,
       not_20_out, not_21_out, not_22_out, not_23_out, not_24_out, not_25_out, not_26_out, not_27_out,
       not_28_out, not_29_out, not_30_out;

  not not_1 (not_1_out, in_1);
  not not_2 (not_2_out, in_2);
  not not_3 (not_3_out, in_3);
  not not_4 (not_4_out, in_2);
  and A_prime_B_prime_C_prime (A_prime_B_prime_C_prime_out, not_1_out, not_2_out, not_3_out);
  and AB_prime_C (AB_prime_C_out, in_1, not_4_out, in_3);
  not not_5 (not_5_out, in_1);
  not not_6 (not_6_out, in_2);
  not not_7 (not_7_out, in_1);
  not not_8 (not_8_out, in_3);
  not not_9 (not_9_out, in_4);
  not not_10 (not_10_out, in_2);
  not not_11 (not_11_out, in_3);
  not not_12 (not_12_out, in_1);
  not not_13 (not_13_out, in_4);
  and A_prime_B_prime (A_prime_B_prime_out, not_5_out, not_6_out);
  and ABCD (ABCD_out, in_1, in_2, in_3, in_4);
  and A_prime_C_prime_D_prime (A_prime_C_prime_D_prime_out, not_7_out, not_8_out, not_9_out);
  and AB_prime_C_prime_D (AB_prime_C_prime_D_out, in_1, not_10_out, not_11_out, in_4);
  and A_prime_BCD_prime (A_prime_BCD_prime_out, not_12_out, in_2, in_3, not_13_out);
  not not_14 (not_14_out, in_1);
  xor A_C (A_C_out, in_1, in_3);
  not not_15 (not_15_out, in_4);
  not not_16 (not_16_out, in_1);
  and A_prime_BC (A_prime_BC_out, not_14_out, in_2, in_3);
  and D_prime_A_C (D_prime_A_C_out, A_C_out, not_15_out);
  and A_prime_BCD (A_prime_BCD_out, not_16_out, in_2, in_3, in_4);
  and CD (CD_out, in_3, in_4);
  not not_17 (not_17_out, in_3);
  and C_prime_D_prime (C_prime_D_prime_out, not_17_out, not_18_out);
  not not_18 (not_18_out, in_4);
  or CD_C_prime_D_prime (CD_C_prime_D_prime_out, CD_out, C_prime_D_prime_out);
  xor B_D (B_D_out, in_2, in_4);
  not not_19 (not_19_out, in_1);
  not not_20 (not_20_out, in_3);
  not not_21 (not_21_out, in_1);
  not not_22 (not_22_out, in_4);
  not not_23 (not_23_out, in_3);
  not not_24 (not_24_out, in_1);
  not not_25 (not_25_out, in_4);
  and AB_CD_C_prime_D_prime (AB_CD_C_prime_D_prime_out, in_1, in_2, CD_C_prime_D_prime_out);
  and A_prime_BC_prime_D (A_prime_BC_prime_D_out, not_19_out, in_2, not_20_out, in_4);
  and A_prime_CD_prime (A_prime_CD_prime_out, not_21_out, in_3, not_22_out);
  and AC_prime_B_D (AC_prime_B_D_out, in_1, not_23_out, B_D_out);
  and A_prime_CD_prime_2 (A_prime_CD_prime_2_out, not_24_out, in_3, not_25_out);
  not not_26 (not_26_out, in_2);
  not not_27 (not_27_out, in_3);
  not ABCD__prime (ABCD__prime_out, ABCD_out);
  and AB_prime_C_prime (AB_prime_C_prime_out, in_1, not_26_out, not_27_out);
  not not_28 (not_28_out, in_4);
  or A_prime_B_prime_C_prime_AB_prime_C (A_prime_B_prime_C_prime_AB_prime_C_out, A_prime_B_prime_C_prime_out, AB_prime_C_out);
  or AB_prime_C_prime_D_A_prime_BCD_prime (AB_prime_C_prime_D_A_prime_BCD_prime_out, AB_prime_C_prime_D_out, A_prime_BCD_prime_out);
  or A_prime_BC_D_prime_A_C (A_prime_BC_D_prime_A_C_out, A_prime_BC_out, D_prime_A_C_out);
  or C_AD__prime___AB_C_prime_D_prime_CD__BD_AC__prime (C_AD__prime___AB_C_prime_D_prime_CD__BD_AC__prime_out, AB_CD_C_prime_D_prime_out, A_prime_BC_prime_D_out, A_prime_CD_prime_out);
  or ABCD_A_prime_B_prime_A_prime_C_prime_D_prime (ABCD_A_prime_B_prime_A_prime_C_prime_D_prime_out, A_prime_B_prime_out, ABCD_out, A_prime_C_prime_D_prime_out);
  or D_prime___AB_prime_C_prime (D_prime___AB_prime_C_prime_out, AB_prime_C_prime_out, not_28_out);
  or A_prime_CD_prime_AC_prime_B_D (A_prime_CD_prime_AC_prime_B_D_out, AC_prime_B_D_out, A_prime_CD_prime_2_out);
  _7_Segment_Display #(.active("false")) u_7_segment_display_1 (
    .g(ABCD_out), .f(ABCD_out), .a(1'b0), .b(ABCD__prime_out),
    .e(ABCD_A_prime_B_prime_A_prime_C_prime_D_prime_out), .d(ABCD_out), .c(1'b0), .dp(not_29_out));
  not not_29 (not_29_out, 1'b0);
  _7_Segment_Display #(.active("false")) u_7_segment_display_2 (
    .g(C_AD__prime___AB_C_prime_D_prime_CD__BD_AC__prime_out), .f(A_prime_BC_D_prime_A_C_out),
    .a(AB_prime_C_prime_D_A_prime_BCD_prime_out), .b(A_prime_B_prime_C_prime_AB_prime_C_out),
    .e(D_prime___AB_prime_C_prime_out), .d(A_prime_CD_prime_AC_prime_B_D_out), .c(A_prime_BCD_out),
    .dp(not_30_out));
  not not_30 (not_30_out, 1'b0);

  // Notes on the sheet:
  //   A
  //   B
  //   C
  //   D
endmodule
