// Logisim project Binary Counter - Both Digits - Enable Bit.circ as structural Verilog: 1 circuit, main circuit main
module main (
  input  enable,
  input  in_2,
  input  in_3,
  input  in_4,
  input  in_5,
  input  in_6,
  input  in_7,
  input  in_8,
  input  in_9,
  input  enable_2
);

  wire A_C_2_out, A_C_out, A_prime_B_prime_2_out, A_prime_B_prime_C_prime_2_out,
       A_prime_B_prime_C_prime_AB_prime_C_2_out, A_prime_B_prime_C_prime_AB_prime_C_out,
       A_prime_B_prime_C_prime_out, A_prime_B_prime_out, A_prime_BC_2_out, A_prime_BC_D_prime_A_C_2_out,
       A_prime_BC_D_prime_A_C_out, A_prime_BC_out, A_prime_BC_prime_D_2_out, A_prime_BC_prime_D_out,
       A_prime_BCD_2_out, A_prime_BCD_out, A_prime_BCD_prime_2_out, A_prime_BCD_prime_out,
       A_prime_C_prime_D_prime_2_out, A_prime_C_prime_D_prime_out, A_prime_CD_prime_2_out,
       A_prime_CD_prime_3_out, A_prime_CD_prime_4_out, A_prime_CD_prime_AC_prime_B_D_2_out,
       A_prime_CD_prime_AC_prime_B_D_out, A_prime_CD_prime_out, AB_CD_C_prime_D_prime_2_out,
       AB_CD_C_prime_D_prime_out, AB_prime_C_2_out, AB_prime_C_out, AB_prime_C_prime_2_out,
       AB_prime_C_prime_D_2_out, AB_prime_C_prime_D_A_prime_BCD_prime_2_out,
       AB_prime_C_prime_D_A_prime_BCD_prime_out, AB_prime_C_prime_D_out, AB_prime_C_prime_out, ABCD_2_out,
       ABCD__prime_2_out, ABCD__prime_out, ABCD_A_prime_B_prime_A_prime_C_prime_D_prime_2_out,
       ABCD_A_prime_B_prime_A_prime_C_prime_D_prime_out, ABCD_out, AC_prime_B_D_2_out, AC_prime_B_D_out,
       B_D_2_out, B_D_out, C_AD__prime___AB_C_prime_D_prime_CD__BD_AC__prime_2_out,
       C_AD__prime___AB_C_prime_D_prime_CD__BD_AC__prime_out, C_prime_D_prime_2_out, C_prime_D_prime_out,
       CD_2_out, CD_C_prime_D_prime_2_out, CD_C_prime_D_prime_out, CD_out, D_prime___AB_prime_C_prime_2_out,
       D_prime___AB_prime_C_prime_out, D_prime_A_C_2_out, D_prime_A_C_out, nand_1_out, nand_2_out,
       nand_3_out, nand_4_out, nand_5_out, nand_6_out, nand_7_out, nand_8_out, nand_9_out, nand_10_out,
       nand_11_out, nand_12_out, nand_13_out, nand_14_out, nand_15_out, nand_16_out, nand_17_out,
       nand_18_out, nand_19_out, nand_20_out, nand_21_out, nand_22_out, nand_23_out, nand_24_out,
       nand_25_out, nand_26_out, nand_27_out, nand_28_out, nand_29_out, nand_30_out, nand_31_out,
       nand_32_out, not_1_out, not_2_out, not_3_out, not_4_out, not_5_out, not_6_out, not_7_out, not_8_out,
       not_9_out, not_10_out, not_11_out, not_12_out, not_13_out, not_14_out, not_15_out, not_16_out,
       not_17_out, not_18_out, not_19_out, not_20_out, not_21_out, not_22_out, not_23_out, not_24_out,
       not_25_out, not_26_out, not_27_out, not_28_out, not_29_out, not_30_out, not_31_out, not_32_out,
       not_33_out, not_34_out, not_35_out, not_36_out, not_37_out, not_38_out, not_39_out, not_40_out,
       not_41_out, not_42_out, not_43_out, not_44_out, not_45_out, not_46_out, not_47_out, not_48_out,
       not_49_out, not_50_out, not_51_out, not_52_out, not_53_out, not_54_out, not_55_out, not_56_out,
       not_57_out, not_58_out, not_59_out, not_60_out, not_61_out, not_62_out, not_63_out, not_64_out,
       not_65_out, not_66_out, not_67_out, not_68_out, not_69_out, not_70_out, not_71_out, not_72_out,
       not_73_out, not_74_out, not_75_out, not_76_out, not_77_out, not_78_out, not_79_out, not_80_out,
       not_81_out, not_82_out, not_83_out, not_84_out;

  not not_1 (not_1_out, in_2);
  not not_2 (not_2_out, in_3);
  and A_prime_B_prime_C_prime (A_prime_B_prime_C_prime_out, not_1_out, not_2_out, not_3_out);
  not not_3 (not_3_out, in_4);
  and AB_prime_C (AB_prime_C_out, in_2, not_4_out, in_4);
  not not_4 (not_4_out, in_3);
  not not_5 (not_5_out, in_2);
  not not_6 (not_6_out, in_6);
  and A_prime_B_prime_C_prime_2 (A_prime_B_prime_C_prime_2_out, not_6_out, not_7_out, not_8_out);
  not not_7 (not_7_out, in_7);
  not not_8 (not_8_out, in_8);
  and AB_prime_C_2 (AB_prime_C_2_out, in_6, not_9_out, in_8);
  not not_9 (not_9_out, in_7);
  not not_10 (not_10_out, in_6);
  and A_prime_BCD (A_prime_BCD_out, not_5_out, in_3, in_4, in_5);
  and A_prime_BCD_2 (A_prime_BCD_2_out, not_10_out, in_7, in_8, in_9);
  not not_11 (not_11_out, in_3);
  not not_12 (not_12_out, in_4);
  not not_13 (not_13_out, in_2);
  not not_14 (not_14_out, in_5);
  not not_15 (not_15_out, in_7);
  not not_16 (not_16_out, in_8);
  not not_17 (not_17_out, in_6);
  not not_18 (not_18_out, in_9);
  and AB_prime_C_prime_D (AB_prime_C_prime_D_out, in_2, not_11_out, not_12_out, in_5);
  and A_prime_BCD_prime (A_prime_BCD_prime_out, not_13_out, in_3, in_4, not_14_out);
  and AB_prime_C_prime_D_2 (AB_prime_C_prime_D_2_out, in_6, not_15_out, not_16_out, in_9);
  and A_prime_BCD_prime_2 (A_prime_BCD_prime_2_out, not_17_out, in_7, in_8, not_18_out);
  not not_19 (not_19_out, in_2);
  xor A_C (A_C_out, in_2, in_4);
  not not_20 (not_20_out, in_5);
  not not_21 (not_21_out, in_4);
  xor B_D (B_D_out, in_3, in_5);
  not not_22 (not_22_out, in_2);
  not not_23 (not_23_out, in_5);
  not not_24 (not_24_out, in_6);
  xor A_C_2 (A_C_2_out, in_6, in_8);
  not not_25 (not_25_out, in_9);
  not not_26 (not_26_out, in_8);
  xor B_D_2 (B_D_2_out, in_7, in_9);
  not not_27 (not_27_out, in_6);
  not not_28 (not_28_out, in_9);
  and A_prime_BC (A_prime_BC_out, not_19_out, in_3, in_4);
  and D_prime_A_C (D_prime_A_C_out, A_C_out, not_20_out);
  not not_29 (not_29_out, in_4);
  not not_30 (not_30_out, in_5);
  and AC_prime_B_D (AC_prime_B_D_out, in_2, not_21_out, B_D_out);
  and A_prime_CD_prime (A_prime_CD_prime_out, not_22_out, in_4, not_23_out);
  and A_prime_BC_2 (A_prime_BC_2_out, not_24_out, in_7, in_8);
  and D_prime_A_C_2 (D_prime_A_C_2_out, A_C_2_out, not_25_out);
  not not_31 (not_31_out, in_8);
  not not_32 (not_32_out, in_9);
  and AC_prime_B_D_2 (AC_prime_B_D_2_out, in_6, not_26_out, B_D_2_out);
  and A_prime_CD_prime_2 (A_prime_CD_prime_2_out, not_27_out, in_8, not_28_out);
  and CD (CD_out, in_4, in_5);
  or CD_C_prime_D_prime (CD_C_prime_D_prime_out, CD_out, C_prime_D_prime_out);
  and C_prime_D_prime (C_prime_D_prime_out, not_29_out, not_30_out);
  and CD_2 (CD_2_out, in_8, in_9);
  or CD_C_prime_D_prime_2 (CD_C_prime_D_prime_2_out, CD_2_out, C_prime_D_prime_2_out);
  and C_prime_D_prime_2 (C_prime_D_prime_2_out, not_31_out, not_32_out);
  not not_33 (not_33_out, in_2);
  not not_34 (not_34_out, in_5);
  not not_35 (not_35_out, in_2);
  not not_36 (not_36_out, in_4);
  not not_37 (not_37_out, in_6);
  not not_38 (not_38_out, in_9);
  not not_39 (not_39_out, in_6);
  not not_40 (not_40_out, in_8);
  and AB_CD_C_prime_D_prime (AB_CD_C_prime_D_prime_out, in_2, in_3, CD_C_prime_D_prime_out);
  and A_prime_CD_prime_3 (A_prime_CD_prime_3_out, not_33_out, in_4, not_34_out);
  and A_prime_BC_prime_D (A_prime_BC_prime_D_out, not_35_out, in_3, not_36_out, in_5);
  and AB_CD_C_prime_D_prime_2 (AB_CD_C_prime_D_prime_2_out, in_6, in_7, CD_C_prime_D_prime_2_out);
  and A_prime_CD_prime_4 (A_prime_CD_prime_4_out, not_37_out, in_8, not_38_out);
  and A_prime_BC_prime_D_2 (A_prime_BC_prime_D_2_out, not_39_out, in_7, not_40_out, in_9);
  not not_41 (not_41_out, in_2);
  not not_42 (not_42_out, in_3);
  not not_43 (not_43_out, in_2);
  not not_44 (not_44_out, in_4);
  not not_45 (not_45_out, in_5);
  not not_46 (not_46_out, in_3);
  and AB_prime_C_prime (AB_prime_C_prime_out, in_2, not_46_out, not_47_out);
  not not_47 (not_47_out, in_4);
  not not_48 (not_48_out, in_5);
  not not_49 (not_49_out, in_6);
  not not_50 (not_50_out, in_7);
  not not_51 (not_51_out, in_6);
  not not_52 (not_52_out, in_8);
  not not_53 (not_53_out, in_9);
  not not_54 (not_54_out, in_7);
  and AB_prime_C_prime_2 (AB_prime_C_prime_2_out, in_6, not_54_out, not_55_out);
  not not_55 (not_55_out, in_8);
  not not_56 (not_56_out, in_9);
  and A_prime_B_prime (A_prime_B_prime_out, not_41_out, not_42_out);
  and ABCD (ABCD_out, in_2, in_3, in_4, in_5);
  and A_prime_C_prime_D_prime (A_prime_C_prime_D_prime_out, not_43_out, not_44_out, not_45_out);
  and A_prime_B_prime_2 (A_prime_B_prime_2_out, not_49_out, not_50_out);
  and ABCD_2 (ABCD_2_out, in_6, in_7, in_8, in_9);
  and A_prime_C_prime_D_prime_2 (A_prime_C_prime_D_prime_2_out, not_51_out, not_52_out, not_53_out);
  or A_prime_B_prime_C_prime_AB_prime_C (A_prime_B_prime_C_prime_AB_prime_C_out, A_prime_B_prime_C_prime_out, AB_prime_C_out);
  or AB_prime_C_prime_D_A_prime_BCD_prime (AB_prime_C_prime_D_A_prime_BCD_prime_out, AB_prime_C_prime_D_out, A_prime_BCD_prime_out);
  or A_prime_BC_D_prime_A_C (A_prime_BC_D_prime_A_C_out, A_prime_BC_out, D_prime_A_C_out);
  or C_AD__prime___AB_C_prime_D_prime_CD__BD_AC__prime (C_AD__prime___AB_C_prime_D_prime_CD__BD_AC__prime_out, AB_CD_C_prime_D_prime_out, A_prime_CD_prime_3_out, A_prime_BC_prime_D_out);
  not ABCD__prime (ABCD__prime_out, ABCD_out);
  or ABCD_A_prime_B_prime_A_prime_C_prime_D_prime (ABCD_A_prime_B_prime_A_prime_C_prime_D_prime_out, A_prime_B_prime_out, ABCD_out, A_prime_C_prime_D_prime_out);
  or D_prime___AB_prime_C_prime (D_prime___AB_prime_C_prime_out, AB_prime_C_prime_out, not_48_out);
  or A_prime_CD_prime_AC_prime_B_D (A_prime_CD_prime_AC_prime_B_D_out, AC_prime_B_D_out, A_prime_CD_prime_out);
  or A_prime_B_prime_C_prime_AB_prime_C_2 (A_prime_B_prime_C_prime_AB_prime_C_2_out, A_prime_B_prime_C_prime_2_out, AB_prime_C_2_out);
  or AB_prime_C_prime_D_A_prime_BCD_prime_2 (AB_prime_C_prime_D_A_prime_BCD_prime_2_out, AB_prime_C_prime_D_2_out, A_prime_BCD_prime_2_out);
  or A_prime_BC_D_prime_A_C_2 (A_prime_BC_D_prime_A_C_2_out, A_prime_BC_2_out, D_prime_A_C_2_out);
  or C_AD__prime___AB_C_prime_D_prime_CD__BD_AC__prime_2 (C_AD__prime___AB_C_prime_D_prime_CD__BD_AC__prime_2_out, AB_CD_C_prime_D_prime_2_out, A_prime_CD_prime_4_out, A_prime_BC_prime_D_2_out);
  not ABCD__prime_2 (ABCD__prime_2_out, ABCD_2_out);
  or ABCD_A_prime_B_prime_A_prime_C_prime_D_prime_2 (ABCD_A_prime_B_prime_A_prime_C_prime_D_prime_2_out, A_prime_B_prime_2_out, ABCD_2_out, A_prime_C_prime_D_prime_2_out);
  or D_prime___AB_prime_C_prime_2 (D_prime___AB_prime_C_prime_2_out, AB_prime_C_prime_2_out, not_56_out);
  or A_prime_CD_prime_AC_prime_B_D_2 (A_prime_CD_prime_AC_prime_B_D_2_out, AC_prime_B_D_2_out, A_prime_CD_prime_2_out);
  not not_57 (not_57_out, 1'b0);
  not not_58 (not_58_out, A_prime_B_prime_C_prime_AB_prime_C_out);
  not not_59 (not_59_out, AB_prime_C_prime_D_A_prime_BCD_prime_out);
  not not_60 (not_60_out, A_prime_BC_D_prime_A_C_out);
  not not_61 (not_61_out, C_AD__prime___AB_C_prime_D_prime_CD__BD_AC__prime_out);
  not not_62 (not_62_out, ABCD__prime_out);
  not not_63 (not_63_out, ABCD_out);
  not not_64 (not_64_out, ABCD_A_prime_B_prime_A_prime_C_prime_D_prime_out);
  not not_65 (not_65_out, ABCD_out);
  not not_66 (not_66_out, D_prime___AB_prime_C_prime_out);
  not not_67 (not_67_out, A_prime_CD_prime_AC_prime_B_D_out);
  not not_68 (not_68_out, A_prime_BCD_out);
  not not_69 (not_69_out, 1'b0);
  not not_70 (not_70_out, A_prime_B_prime_C_prime_AB_prime_C_2_out);
  not not_71 (not_71_out, AB_prime_C_prime_D_A_prime_BCD_prime_2_out);
  not not_72 (not_72_out, A_prime_BC_D_prime_A_C_2_out);
  not not_73 (not_73_out, C_AD__prime___AB_C_prime_D_prime_CD__BD_AC__prime_2_out);
  not not_74 (not_74_out, ABCD__prime_2_out);
  not not_75 (not_75_out, ABCD_2_out);
  not not_76 (not_76_out, ABCD_A_prime_B_prime_A_prime_C_prime_D_prime_2_out);
  not not_77 (not_77_out, ABCD_2_out);
  not not_78 (not_78_out, D_prime___AB_prime_C_prime_2_out);
  not not_79 (not_79_out, A_prime_CD_prime_AC_prime_B_D_2_out);
  not not_80 (not_80_out, A_prime_BCD_2_out);
  nand nand_1 (nand_1_out, not_57_out, enable);
  nand nand_2 (nand_2_out, not_63_out, enable);
  nand nand_3 (nand_3_out, enable, not_63_out);
  _7_Segment_Display #(.active("false")) u_7_segment_display_1 (
    .g(nand_2_out), .f(nand_3_out), .a(nand_1_out), .b(nand_13_out), .e(nand_6_out), .d(nand_5_out),
    .c(nand_4_out), .dp(nand_14_out));
  nand nand_4 (nand_4_out, not_57_out, enable);
  nand nand_5 (nand_5_out, enable, not_65_out);
  nand nand_6 (nand_6_out, not_64_out, enable);
  nand nand_7 (nand_7_out, not_69_out, enable_2);
  nand nand_8 (nand_8_out, not_75_out, enable_2);
  nand nand_9 (nand_9_out, enable_2, not_75_out);
  _7_Segment_Display #(.active("false")) u_7_segment_display_2 (
    .g(nand_8_out), .f(nand_9_out), .a(nand_7_out), .b(nand_15_out), .e(nand_10_out), .d(nand_11_out),
    .c(nand_12_out), .dp(nand_16_out));
  nand nand_10 (nand_10_out, not_76_out, enable_2);
  nand nand_11 (nand_11_out, enable_2, not_77_out);
  nand nand_12 (nand_12_out, not_69_out, enable_2);
  nand nand_13 (nand_13_out, enable, not_62_out);
  nand nand_14 (nand_14_out, enable, not_81_out);
  not not_81 (not_81_out, not_57_out);
  nand nand_15 (nand_15_out, enable_2, not_74_out);
  nand nand_16 (nand_16_out, enable_2, not_82_out);
  not not_82 (not_82_out, not_69_out);
  nand nand_17 (nand_17_out, enable, not_60_out);
  nand nand_18 (nand_18_out, not_59_out, enable);
  nand nand_19 (nand_19_out, not_61_out, enable);
  _7_Segment_Display #(.active("false")) u_7_segment_display_3 (
    .g(nand_19_out), .f(nand_17_out), .a(nand_18_out), .b(nand_29_out), .e(nand_22_out), .d(nand_20_out),
    .c(nand_21_out), .dp(nand_30_out));
  nand nand_20 (nand_20_out, enable, not_67_out);
  nand nand_21 (nand_21_out, not_68_out, enable);
  nand nand_22 (nand_22_out, not_66_out, enable);
  nand nand_23 (nand_23_out, not_71_out, enable_2);
  nand nand_24 (nand_24_out, not_73_out, enable_2);
  nand nand_25 (nand_25_out, enable_2, not_72_out);
  _7_Segment_Display #(.active("false")) u_7_segment_display_4 (
    .g(nand_24_out), .f(nand_25_out), .a(nand_23_out), .b(nand_31_out), .e(nand_27_out), .d(nand_26_out),
    .c(nand_28_out), .dp(nand_32_out));
  nand nand_26 (nand_26_out, enable_2, not_79_out);
  nand nand_27 (nand_27_out, not_78_out, enable_2);
  nand nand_28 (nand_28_out, not_80_out, enable_2);
  nand nand_29 (nand_29_out, enable, not_58_out);
  nand nand_30 (nand_30_out, enable, not_83_out);
  not not_83 (not_83_out, not_57_out);
  nand nand_31 (nand_31_out, enable_2, not_70_out);
  nand nand_32 (nand_32_out, enable_2, not_84_out);
  not not_84 (not_84_out, not_69_out);

  // Notes on the sheet:
  //   bit
  //   A
  //   B
  //   C
  //   D
  //   A
  //   B
  //   C
  //   D
  //   A   B   C   D
  //   A
  //   B
  //   C
  //   D
  //   bit
endmodule
