// Logisim project Binary Counter - Both Digits - Organised.circ as structural Verilog: 1 circuit, main circuit main
module main (
  input  in_1,
  input  in_2,
  input  in_3,
  input  in_4,
  input  in_5,
  input  in_6,
  input  in_7,
  input  in_8
);

  wire A_C_2_out, A_C_out, A_prime_B_prime_2_out, A_prime_B_prime_C_prime_2_out,
       A_prime_B_prime_C_prime_AB_prime_C_2_out, A_prime_B_prime_C_prime_AB_prime_C_out,
       A_prime_B_prime_C_prime_out, A_prime_B_prime_out, A_prime_BC_2_out, A_prime_BC_D_prime_A_C_2_out,
       A_prime_BC_D_prime_A_C_out, A_prime_BC_out, A_prime_BC_prime_D_2_out, A_prime_BC_prime_D_out,
       A_prime_BCD_2_out, A_prime_BCD_out, A_prime_BCD_prime_2_out, A_prime_BCD_prime_out,
       A_prime_C_prime_D_prime_2_out, A_prime_C_prime_D_prime_out, A_prime_CD_prime_2_out,
       A_prime_CD_prime_3_out, A_prime_CD_prime_4_out, A_prime_CD_prime_AC_prime_B_D_2_out,
       A_prime_CD_prime_AC_prime_B_D_out, A_prime_CD_prime_out, AB_CD_C_prime_D_prime_2_out,
       AB_CD_C_prime_D_prime_out, AB_prime_C_2_out, AB_prime_C_out, AB_prime_C_prime_2_out,
       AB_prime_C_prime_D_2_out, AB_prime_C_prime_D_A_prime_BCD_prime_2_out,
       AB_prime_C_prime_D_A_prime_BCD_prime_out, AB_prime_C_prime_D_out, AB_prime_C_prime_out, ABCD_2_out,
       ABCD__prime_2_out, ABCD__prime_out, ABCD_A_prime_B_prime_A_prime_C_prime_D_prime_2_out,
       ABCD_A_prime_B_prime_A_prime_C_prime_D_prime_out, ABCD_out, AC_prime_B_D_2_out, AC_prime_B_D_out,
       B_D_2_out, B_D_out, C_AD__prime___AB_C_prime_D_prime_CD__BD_AC__prime_2_out,
       C_AD__prime___AB_C_prime_D_prime_CD__BD_AC__prime_out, C_prime_D_prime_2_out, C_prime_D_prime_out,
       CD_2_out, CD_C_prime_D_prime_2_out, CD_C_prime_D_prime_out, CD_out, D_prime___AB_prime_C_prime_2_out,
       D_prime___AB_prime_C_prime_out, D_prime_A_C_2_out, D_prime_A_C_out, not_1_out, not_2_out, not_3_out,
       not_4_out, not_5_out, not_6_out, not_7_out, not_8_out, not_9_out, not_10_out, not_11_out, not_12_out,
       not_13_out, not_14_out, not_15_out, not_16_out, not_17_out, not_18_out, not_19_out, not_20_out,
       not_21_out, not_22_out, not_23_out, not_24_out, not_25_out, not_26_out, not_27_out, not_28_out,
       not_29_out, not_30_out, not_31_out, not_32_out, not_33_out, not_34_out, not_35_out, not_36_out,
       not_37_out, not_38_out, not_39_out, not_40_out, not_41_out, not_42_out, not_43_out, not_44_out,
       not_45_out, not_46_out, not_47_out, not_48_out, not_49_out, not_50_out, not_51_out, not_52_out,
       not_53_out, not_54_out, not_55_out, not_56_out, not_57_out, not_58_out, not_59_out, not_60_out;

  not not_1 (not_1_out, in_1);
  not not_2 (not_2_out, in_3);
  not not_3 (not_3_out, in_2);
  not not_4 (not_4_out, in_1);
  not not_5 (not_5_out, in_2);
  and A_prime_BCD (A_prime_BCD_out, not_1_out, in_2, in_3, in_4);
  and A_prime_B_prime_C_prime (A_prime_B_prime_C_prime_out, not_2_out, not_3_out, not_4_out);
  and AB_prime_C (AB_prime_C_out, in_3, not_5_out, in_1);
  not not_6 (not_6_out, in_3);
  not not_7 (not_7_out, in_2);
  not not_8 (not_8_out, in_4);
  not not_9 (not_9_out, in_1);
  not not_10 (not_10_out, in_5);
  and A_prime_B_prime_C_prime_2 (A_prime_B_prime_C_prime_2_out, not_10_out, not_11_out, not_12_out);
  not not_11 (not_11_out, in_6);
  not not_12 (not_12_out, in_7);
  not not_13 (not_13_out, in_6);
  and AB_prime_C_2 (AB_prime_C_2_out, in_5, not_13_out, in_7);
  not not_14 (not_14_out, in_5);
  and AB_prime_C_prime_D (AB_prime_C_prime_D_out, in_4, not_6_out, not_7_out, in_1);
  and A_prime_BCD_prime (A_prime_BCD_prime_out, not_8_out, in_3, in_2, not_9_out);
  and A_prime_BCD_2 (A_prime_BCD_2_out, not_14_out, in_6, in_7, in_8);
  xor B_D (B_D_out, in_2, in_4);
  not not_15 (not_15_out, in_6);
  not not_16 (not_16_out, in_7);
  not not_17 (not_17_out, in_5);
  not not_18 (not_18_out, in_8);
  not not_19 (not_19_out, in_4);
  xor A_C (A_C_out, in_4, in_2);
  not not_20 (not_20_out, in_1);
  not not_21 (not_21_out, in_3);
  and AC_prime_B_D (AC_prime_B_D_out, in_1, not_21_out, B_D_out);
  not not_22 (not_22_out, in_1);
  and A_prime_CD_prime (A_prime_CD_prime_out, not_22_out, in_3, not_23_out);
  not not_23 (not_23_out, in_4);
  and AB_prime_C_prime_D_2 (AB_prime_C_prime_D_2_out, in_5, not_15_out, not_16_out, in_8);
  and A_prime_BCD_prime_2 (A_prime_BCD_prime_2_out, not_17_out, in_6, in_7, not_18_out);
  and A_prime_BC (A_prime_BC_out, not_19_out, in_3, in_2);
  and D_prime_A_C (D_prime_A_C_out, A_C_out, not_20_out);
  not not_24 (not_24_out, in_5);
  xor A_C_2 (A_C_2_out, in_5, in_7);
  not not_25 (not_25_out, in_8);
  not not_26 (not_26_out, in_7);
  xor B_D_2 (B_D_2_out, in_6, in_8);
  not not_27 (not_27_out, in_5);
  not not_28 (not_28_out, in_8);
  and CD (CD_out, in_2, in_1);
  not not_29 (not_29_out, in_2);
  and C_prime_D_prime (C_prime_D_prime_out, not_29_out, not_30_out);
  not not_30 (not_30_out, in_1);
  and A_prime_BC_2 (A_prime_BC_2_out, not_24_out, in_6, in_7);
  and D_prime_A_C_2 (D_prime_A_C_2_out, A_C_2_out, not_25_out);
  and CD_2 (CD_2_out, in_7, in_8);
  not not_31 (not_31_out, in_7);
  not not_32 (not_32_out, in_8);
  and AC_prime_B_D_2 (AC_prime_B_D_2_out, in_5, not_26_out, B_D_2_out);
  and A_prime_CD_prime_2 (A_prime_CD_prime_2_out, not_27_out, in_7, not_28_out);
  or CD_C_prime_D_prime (CD_C_prime_D_prime_out, CD_out, C_prime_D_prime_out);
  and AB_prime_C_prime (AB_prime_C_prime_out, in_1, not_33_out, not_34_out);
  not not_33 (not_33_out, in_2);
  not not_34 (not_34_out, in_3);
  not not_35 (not_35_out, in_4);
  or CD_C_prime_D_prime_2 (CD_C_prime_D_prime_2_out, CD_2_out, C_prime_D_prime_2_out);
  and C_prime_D_prime_2 (C_prime_D_prime_2_out, not_31_out, not_32_out);
  and AB_CD_C_prime_D_prime (AB_CD_C_prime_D_prime_out, in_4, in_3, CD_C_prime_D_prime_out);
  not not_36 (not_36_out, in_4);
  and A_prime_BC_prime_D (A_prime_BC_prime_D_out, not_36_out, in_3, not_37_out, in_1);
  not not_37 (not_37_out, in_2);
  not not_38 (not_38_out, in_4);
  and A_prime_CD_prime_3 (A_prime_CD_prime_3_out, not_38_out, in_2, not_39_out);
  not not_39 (not_39_out, in_1);
  not not_40 (not_40_out, in_5);
  not not_41 (not_41_out, in_8);
  not not_42 (not_42_out, in_5);
  not not_43 (not_43_out, in_7);
  not not_44 (not_44_out, in_1);
  not not_45 (not_45_out, in_2);
  not not_46 (not_46_out, in_1);
  not not_47 (not_47_out, in_3);
  not not_48 (not_48_out, in_4);
  and AB_CD_C_prime_D_prime_2 (AB_CD_C_prime_D_prime_2_out, in_5, in_6, CD_C_prime_D_prime_2_out);
  and A_prime_CD_prime_4 (A_prime_CD_prime_4_out, not_40_out, in_7, not_41_out);
  and A_prime_BC_prime_D_2 (A_prime_BC_prime_D_2_out, not_42_out, in_6, not_43_out, in_8);
  and A_prime_B_prime (A_prime_B_prime_out, not_44_out, not_45_out);
  and ABCD (ABCD_out, in_1, in_2, in_3, in_4);
  and A_prime_C_prime_D_prime (A_prime_C_prime_D_prime_out, not_46_out, not_47_out, not_48_out);
  not not_49 (not_49_out, in_5);
  not not_50 (not_50_out, in_6);
  not not_51 (not_51_out, in_5);
  not not_52 (not_52_out, in_7);
  not not_53 (not_53_out, in_8);
  not not_54 (not_54_out, in_6);
  and AB_prime_C_prime_2 (AB_prime_C_prime_2_out, in_5, not_54_out, not_55_out);
  not not_55 (not_55_out, in_7);
  not not_56 (not_56_out, in_8);
  not ABCD__prime (ABCD__prime_out, ABCD_out);
  and A_prime_B_prime_2 (A_prime_B_prime_2_out, not_49_out, not_50_out);
  and ABCD_2 (ABCD_2_out, in_5, in_6, in_7, in_8);
  and A_prime_C_prime_D_prime_2 (A_prime_C_prime_D_prime_2_out, not_51_out, not_52_out, not_53_out);
  or A_prime_B_prime_C_prime_AB_prime_C (A_prime_B_prime_C_prime_AB_prime_C_out, A_prime_B_prime_C_prime_out, AB_prime_C_out);
  or AB_prime_C_prime_D_A_prime_BCD_prime (AB_prime_C_prime_D_A_prime_BCD_prime_out, AB_prime_C_prime_D_out, A_prime_BCD_prime_out);
  or A_prime_BC_D_prime_A_C (A_prime_BC_D_prime_A_C_out, A_prime_BC_out, D_prime_A_C_out);
  or C_AD__prime___AB_C_prime_D_prime_CD__BD_AC__prime (C_AD__prime___AB_C_prime_D_prime_CD__BD_AC__prime_out, AB_CD_C_prime_D_prime_out, A_prime_BC_prime_D_out, A_prime_CD_prime_3_out);
  _7_Segment_Display #(.active("false")) u_7_segment_display_1 (
    .g(ABCD_out), .f(ABCD_out), .a(1'b0), .b(ABCD__prime_out),
    .e(ABCD_A_prime_B_prime_A_prime_C_prime_D_prime_out), .d(ABCD_out), .c(1'b0), .dp(not_57_out));
  or ABCD_A_prime_B_prime_A_prime_C_prime_D_prime (ABCD_A_prime_B_prime_A_prime_C_prime_D_prime_out, A_prime_B_prime_out, ABCD_out, A_prime_C_prime_D_prime_out);
  or D_prime___AB_prime_C_prime (D_prime___AB_prime_C_prime_out, AB_prime_C_prime_out, not_35_out);
  or A_prime_CD_prime_AC_prime_B_D (A_prime_CD_prime_AC_prime_B_D_out, AC_prime_B_D_out, A_prime_CD_prime_out);
  or A_prime_B_prime_C_prime_AB_prime_C_2 (A_prime_B_prime_C_prime_AB_prime_C_2_out, A_prime_B_prime_C_prime_2_out, AB_prime_C_2_out);
  or AB_prime_C_prime_D_A_prime_BCD_prime_2 (AB_prime_C_prime_D_A_prime_BCD_prime_2_out, AB_prime_C_prime_D_2_out, A_prime_BCD_prime_2_out);
  or A_prime_BC_D_prime_A_C_2 (A_prime_BC_D_prime_A_C_2_out, A_prime_BC_2_out, D_prime_A_C_2_out);
  or C_AD__prime___AB_C_prime_D_prime_CD__BD_AC__prime_2 (C_AD__prime___AB_C_prime_D_prime_CD__BD_AC__prime_2_out, AB_CD_C_prime_D_prime_2_out, A_prime_CD_prime_4_out, A_prime_BC_prime_D_2_out);
  not ABCD__prime_2 (ABCD__prime_2_out, ABCD_2_out);
  or ABCD_A_prime_B_prime_A_prime_C_prime_D_prime_2 (ABCD_A_prime_B_prime_A_prime_C_prime_D_prime_2_out, A_prime_B_prime_2_out, ABCD_2_out, A_prime_C_prime_D_prime_2_out);
  or D_prime___AB_prime_C_prime_2 (D_prime___AB_prime_C_prime_2_out, AB_prime_C_prime_2_out, not_56_out);
  or A_prime_CD_prime_AC_prime_B_D_2 (A_prime_CD_prime_AC_prime_B_D_2_out, AC_prime_B_D_2_out, A_prime_CD_prime_2_out);
  not not_57 (not_57_out, 1'b0);
  _7_Segment_Display #(.active("false")) u_7_segment_display_2 (
    .g(C_AD__prime___AB_C_prime_D_prime_CD__BD_AC__prime_out), .f(A_prime_BC_D_prime_A_C_out),
    .a(AB_prime_C_prime_D_A_prime_BCD_prime_out), .b(A_prime_B_prime_C_prime_AB_prime_C_out),
    .e(D_prime___AB_prime_C_prime_out), .d(A_prime_CD_prime_AC_prime_B_D_out), .c(A_prime_BCD_out),
    .dp(not_58_out));
  not not_58 (not_58_out, 1'b0);
  _7_Segment_Display #(.active("false")) u_7_segment_display_3 (
    .g(ABCD_2_out), .f(ABCD_2_out), .a(1'b0), .b(ABCD__prime_2_out),
    .e(ABCD_A_prime_B_prime_A_prime_C_prime_D_prime_2_out), .d(ABCD_2_out), .c(1'b0), .dp(not_59_out));
  not not_59 (not_59_out, 1'b0);
  _7_Segment_Display #(.active("false")) u_7_segment_display_4 (
    .g(C_AD__prime___AB_C_prime_D_prime_CD__BD_AC__prime_2_out), .f(A_prime_BC_D_prime_A_C_2_out),
    .a(AB_prime_C_prime_D_A_prime_BCD_prime_2_out), .b(A_prime_B_prime_C_prime_AB_prime_C_2_out),
    .e(D_prime___AB_prime_C_prime_2_out), .d(A_prime_CD_prime_AC_prime_B_D_2_out), .c(A_prime_BCD_2_out),
    .dp(not_60_out));
  not not_60 (not_60_out, 1'b0);

  // Notes on the sheet:
  //   A
  //   B
  //   C
  //   D
  //   A
  //   B
  //   C
  //   D
endmodule
