// Logisim project Binary Counter - Digit #1.circ as structural Verilog: 1 circuit, main circuit main
module main (
  input  in_1,
  input  in_2,
  input  in_3,
  input  in_4,
  input  in_5,
  input  in_6,
  input  in_7,
  input  in_8
);

  wire _1_out, A_prime_B_prime_out, A_prime_C_prime_D_prime_out, ABCD__prime_out,
       ABCD_A_prime_B_prime_A_prime_C_prime_D_prime_out, ABCD_out, and_1_out, and_2_out, and_3_out,
       not_1_out, not_2_out, not_3_out, not_4_out, not_5_out, not_6_out, not_7_out, not_8_out, not_9_out,
       not_10_out, not_11_out, not_12_out, or_1_out;

  not not_1 (not_1_out, 1'b1);
  not not_2 (not_2_out, in_1);
  not not_3 (not_3_out, in_2);
  and and_1 (and_1_out, in_1, in_2, in_3, in_4);
  and and_2 (and_2_out, not_2_out, not_3_out);
  not not_4 (not_4_out, in_1);
  and and_3 (and_3_out, not_4_out, not_5_out, not_6_out);
  not not_5 (not_5_out, in_3);
  not not_6 (not_6_out, in_4);
  not not_7 (not_7_out, in_5);
  not not_8 (not_8_out, in_6);
  not not_9 (not_9_out, in_5);
  not not_10 (not_10_out, in_7);
  not not_11 (not_11_out, in_8);
  not not_12 (not_12_out, and_1_out);
  and ABCD (ABCD_out, in_5, in_6, in_7, in_8);
  and A_prime_B_prime (A_prime_B_prime_out, not_7_out, not_8_out);
  and A_prime_C_prime_D_prime (A_prime_C_prime_D_prime_out, not_9_out, not_10_out, not_11_out);
  or or_1 (or_1_out, and_1_out, and_2_out, and_3_out);
  not ABCD__prime (ABCD__prime_out, ABCD_out);
  or ABCD_A_prime_B_prime_A_prime_C_prime_D_prime (ABCD_A_prime_B_prime_A_prime_C_prime_D_prime_out, ABCD_out, A_prime_B_prime_out, A_prime_C_prime_D_prime_out);
  _7_Segment_Display #(.active("false")) u_7_segment_display_1 (
    .g(and_1_out), .f(and_1_out), .a(not_1_out), .b(not_12_out), .e(or_1_out), .d(and_1_out), .c(not_1_out),
    .dp(1'b1));
  _7_Segment_Display #(.active("false")) u_7_segment_display_2 (
    .g(ABCD_out), .f(ABCD_out), .a(1'b0), .b(ABCD__prime_out),
    .e(ABCD_A_prime_B_prime_A_prime_C_prime_D_prime_out), .d(ABCD_out), .c(1'b0), .dp(_1_out));
  not _1 (_1_out, 1'b0);
endmodule
