// Logisim project Binary Counter - Figuring Out Enable Bit.circ as structural Verilog: 1 circuit, main circuit main
module main (
  input  EB,
  input  in_2,
  input  in_3,
  input  EB_2,
  input  A,
  input  in_6,
  input  in_7,
  input  in_8,
  input  in_9,
  input  EB_3,
  input  in_11,
  input  in_12
);

  wire A_EB__prime_out, and_1_out, and_2_out, and_3_out, and_4_out, and_5_out, and_6_out,
       EB_prime___A_prime_out, nand_1_out, nand_2_out, nand_3_out, nand_4_out, nand_5_out, nand_6_out,
       nand_7_out, nand_8_out, not_1_out, not_2_out, not_3_out, not_4_out, not_5_out, not_6_out, not_7_out,
       not_8_out, not_9_out, not_10_out, not_11_out, not_12_out, not_13_out, not_14_out, not_15_out,
       not_16_out, not_17_out, not_18_out, not_19_out, not_20_out, not_21_out, not_22_out, not_23_out,
       not_24_out, not_25_out, not_26_out, not_27_out, not_28_out, not_29_out, not_30_out, not_31_out,
       or_1_out, or_2_out, or_3_out, or_4_out, or_5_out, or_6_out, or_7_out, or_8_out, or_9_out, or_10_out;

  not not_1 (not_1_out, in_2);
  not not_2 (not_2_out, in_6);
  not not_3 (not_3_out, in_7);
  not not_4 (not_4_out, in_8);
  not not_5 (not_5_out, in_11);
  not not_6 (not_6_out, in_12);
  and and_1 (and_1_out, in_2, in_3, in_6, in_7);
  not not_7 (not_7_out, in_2);
  and and_2 (and_2_out, not_7_out, not_8_out);
  not not_8 (not_8_out, in_3);
  and and_3 (and_3_out, not_1_out, not_2_out, not_3_out);
  and and_4 (and_4_out, in_8, in_9, in_11, in_12);
  not not_9 (not_9_out, in_8);
  and and_5 (and_5_out, not_9_out, not_10_out);
  not not_10 (not_10_out, in_9);
  and and_6 (and_6_out, not_4_out, not_5_out, not_6_out);
  not not_11 (not_11_out, and_1_out);
  not not_12 (not_12_out, and_4_out);
  or or_1 (or_1_out, and_1_out, and_2_out, and_3_out);
  or or_2 (or_2_out, and_4_out, and_5_out, and_6_out);
  not not_13 (not_13_out, and_1_out);
  nand nand_1 (nand_1_out, not_13_out, EB_2);
  _7_Segment_Display #(.active("false")) u_7_segment_display_1 (
    .g(nand_1_out), .f(nand_3_out), .a(nand_5_out), .b(nand_4_out), .e(nand_2_out), .d(nand_8_out),
    .c(nand_6_out), .dp(nand_7_out));
  nand nand_2 (nand_2_out, not_14_out, EB_2);
  not not_14 (not_14_out, or_1_out);
  not not_15 (not_15_out, and_4_out);
  or or_3 (or_3_out, not_15_out, not_16_out);
  _7_Segment_Display #(.active("false")) u_7_segment_display_2 (
    .g(or_3_out), .f(or_5_out), .a(or_7_out), .b(or_6_out), .e(or_4_out), .d(or_9_out), .c(or_10_out),
    .dp(or_8_out));
  not not_16 (not_16_out, EB_3);
  or or_4 (or_4_out, not_17_out, not_16_out);
  not not_17 (not_17_out, or_2_out);
  not not_18 (not_18_out, not_11_out);
  not not_19 (not_19_out, and_1_out);
  not not_20 (not_20_out, 1'b0);
  nand nand_3 (nand_3_out, EB_2, not_19_out);
  nand nand_4 (nand_4_out, EB_2, not_18_out);
  nand nand_5 (nand_5_out, not_20_out, EB_2);
  nand nand_6 (nand_6_out, not_21_out, EB_2);
  nand nand_7 (nand_7_out, EB_2, 1'b0);
  nand nand_8 (nand_8_out, EB_2, not_22_out);
  not not_21 (not_21_out, 1'b0);
  not not_22 (not_22_out, and_1_out);
  not not_23 (not_23_out, not_12_out);
  not not_24 (not_24_out, 1'b0);
  not not_25 (not_25_out, and_4_out);
  or or_5 (or_5_out, not_16_out, not_25_out);
  or or_6 (or_6_out, not_16_out, not_23_out);
  or or_7 (or_7_out, not_24_out, not_16_out);
  or or_8 (or_8_out, not_16_out, not_28_out);
  or or_9 (or_9_out, not_16_out, not_26_out);
  or or_10 (or_10_out, not_27_out, not_16_out);
  not not_26 (not_26_out, and_4_out);
  not not_27 (not_27_out, 1'b0);
  not not_28 (not_28_out, not_29_out);
  not not_29 (not_29_out, 1'b0);
  not not_30 (not_30_out, EB);
  not not_31 (not_31_out, A);
  or EB_prime___A_prime (EB_prime___A_prime_out, not_30_out, not_31_out);
  LED #(.active("false")) led_1 (.in(EB_prime___A_prime_out));
  nand A_EB__prime (A_EB__prime_out, EB, A);
  LED #(.active("false")) led_2 (.in(A_EB__prime_out));

  // Notes on the sheet:
  //   Use (A'*EB)'
  //   Use A'+EB'
endmodule
